// Logisim project ex1.circ as structural Verilog: 1 circuit, main circuit generate_immediate
module generate_immediate (
  input  [31:0] INSTRUCTION,
  output [31:0] IMMEDIATE
);

  Multiplexer #(.enable("false"), .width(20)) multiplexer_1 (
    .in0({20{1'b0}}), .in1({20{1'b1}}), .out(IMMEDIATE[31:12]), .sel(INSTRUCTION[31]));

  assign IMMEDIATE[11:0] = {INSTRUCTION[31:25], INSTRUCTION[11:7]};

  // Other names for the same wires on the sheet: inimm[31:0] = INSTRUCTION;
  //   outimm[31:0] = {IMMEDIATE[31:12], INSTRUCTION[31:25], INSTRUCTION[11:7]}
endmodule
