// Logisim project ex2.circ as structural Verilog: 1 circuit, main circuit compute_BrUn
module compute_BrUn (
  input  [31:0] INSTRUCTION,
  output BrUn
);

  Multiplexer #(.enable("false"), .select(3)) multiplexer_1 (
    .in0(1'b0), .in1(1'b0), .in2(1'b0), .in3(1'b0), .in4(1'b0), .in5(1'b0), .in6(1'b1), .in7(1'b1),
    .out(BrUn), .sel(INSTRUCTION[14:12]));
  Comparator #(.width(5)) comparator_1 (.a(INSTRUCTION[19:15]), .b(INSTRUCTION[24:20]));  // open: gt, eq, lt

  // Other names for the same wires on the sheet: BrUn_In[31:0] = INSTRUCTION; opcode[6:0] = INSTRUCTION[6:0];
  //   funct3[2:0] = INSTRUCTION[14:12]; rs1[4:0] = INSTRUCTION[19:15]; rs2[4:0] = INSTRUCTION[24:20]; BrUn_Out = BrUn;
  //   imm0_11[11:0] = {INSTRUCTION[31], INSTRUCTION[7], INSTRUCTION[30:25], INSTRUCTION[11:8]};
  //   imm4_1[3:0] = INSTRUCTION[11:8]; imm5_10[5:0] = INSTRUCTION[30:25]; imm11 = INSTRUCTION[7];
  //   imm12 = INSTRUCTION[31]
endmodule
